# Fritzing sketch upy-door-sensor (saved by Fritzing 0.9.4)
circuit board: 3.79426cm x 1.86025cm
breadboards: 1

parts:
  U1 = ESP8266 WiFi Module [part_number=ESP01S]
  R1 = Resistor [tolerance=±5% resistance=100k package=THT]
  R3 = Resistor [tolerance=±5% resistance=330 package=THT]
  Q1 = NPN-Transistor [part_number=BC547 package="TO92 [THT]"]
  R2 = Resistor [tolerance=±5% resistance=10k package=THT]
  JP1 = Header 3 [package=screwterminal-3.5mm-3_lock.007s]
  IC1 = Voltage Regulator [package=to-92]
  JP2 = mystery part, 2 pins [chip_label=?]
  C1 = Film/Foil Capacitor [capacitance=100nF voltage=35V package="5mm [THT, pp]"]
  C2 = Capacitor Polarized [package=cpol-radial-1000uf-25v]

nets:
  N1: U1.VCC, JP1.2, JP1.3, IC1.OUT, C2.+
  N2: U1.RST, Q1.C
  GND: U1.GND, R1.Pin_0, Q1.E, R2.Pin_0, IC1.GND, JP2.pin2, C2.-
  N3: R1.Pin_1, JP1.1, C1.-
  N4: R3.Pin_0, R2.Pin_1, C1.+
  N5: R3.Pin_1, Q1.B
  N6: IC1.IN, JP2.pin1

notes:
  (+)(-)
  HT7330-A

custom parts:
  ESP8266 WiFi Module: Generic WiFi Module based on the ESP8266 with onboard PCB antenna and UART communications
